# Fritzing sketch Replik84j (saved by Fritzing 0.9.3b)
breadboards: 1

parts:
  R1 = Temperature Sensor (Thermistor) [thermistor_type=NTC part_number=NozTherm package=THT]
  Nozzle_Heater = Resistor [tolerance=±5% resistance=3.6 package=THT]
  Q1 = MOSFET-NCHANNEL [package=to-92]
  Raspberry_Pi_3_Model_b = Raspberry Pi 3 [part_number=RPI-3-V1.2]
  R2 = Resistor [tolerance=±5% resistance=10k package=THT]
  ADC = IC, DIP package, 16 pins [chip_label=PFC8591]
  R3 = Resistor [tolerance=±5% resistance=10k package=THT]
  R4 = Resistor [tolerance=±5% resistance=10k package=THT]
  HeadBed_A = Resistor [tolerance=±5% resistance=3.6 package=THT]
  HeadBed_B = Resistor [tolerance=±5% resistance=3.6 package=THT]
  Q2 = MOSFET-NCHANNEL [package=to-92]
  Q3 = MOSFET-NCHANNEL [package=to-92]
  R5 = Resistor [tolerance=±5% resistance=10k package=THT]
  R6 = Resistor [tolerance=±5% resistance=10k package=THT]
  R7 = Temperature Sensor (Thermistor) [thermistor_type=NTC part_number=BedATherm package=THT]
  R8 = Temperature Sensor (Thermistor) [thermistor_type=NTC part_number=BedBTherm package=THT]
  R9 = Resistor [tolerance=±5% resistance=10k package=THT]
  R10 = Resistor [tolerance=±5% resistance=10k package=THT]
  R11 = Resistor [tolerance=±5% resistance=10k package=THT]
  Pololu_A6 = DRV 8825 Stepper Motor Carrier, High Current [part_number="DRV 8825 x"]
  Y5 = Stepper Motor - Bipolar
  Pololu_A7 = DRV 8825 Stepper Motor Carrier, High Current [part_number="DRV 8825 y"]
  Y6 = Stepper Motor - Bipolar
  Pololu_A8 = DRV 8825 Stepper Motor Carrier, High Current [part_number="DRV 8825 e"]
  Pololu_A9 = DRV 8825 Stepper Motor Carrier, High Current [part_number="DRV 8825 z"]
  Y7 = Stepper Motor - Bipolar
  Y8 = Stepper Motor - Bipolar
  R12 = Resistor [tolerance=±5% resistance=10k package=THT]
  R13 = Resistor [tolerance=±5% resistance=10k package=THT]
  R14 = Resistor [tolerance=±5% resistance=10k package=THT]
  R15 = Resistor [tolerance=±5% resistance=10k package=THT]
  R16 = Resistor [tolerance=±5% resistance=10k package=THT]
  R17 = Resistor [tolerance=±5% resistance=10k package=THT]
  S1 = SPST Switch [package=switch-spdt-smd]
  S2 = SPST Switch [package=switch-spdt-smd]
  S3 = SPST Switch [package=switch-spdt-smd]
  S4 = SPST Switch [package=switch-spdt-smd]
  S5 = SPST Switch [package=switch-spdt-smd]
  S6 = SPST Switch [package=switch-spdt-smd]
  U3 = 74HC595 SMD [package="SO16 [SMD]"]
  U4 = 74HC595 SMD [package="SO16 [SMD]"]

nets:
  GND: R1.pin_0, Raspberry_Pi_3_Model_b.GND, R2.Pin_0, ADC.pin1, ADC.pin2, ADC.pin3, ADC.pin4, ADC.pin12, ADC.pin13, Q2.S, Q3.S, R5.Pin_0, R6.Pin_0, R7.pin_0, R8.pin_0, Pololu_A6.GROUND_ST/_MT, Pololu_A6.GROUND_LOG, Pololu_A7.GROUND_ST/_MT, Pololu_A7.GROUND_LOG, Pololu_A8.GROUND_ST/_MT, Pololu_A8.GROUND_LOG, Pololu_A9.GROUND_ST/_MT, Pololu_A9.GROUND_LOG, S1.S, U3.GND, U3.OE, U4.GND, U4.Q0
  N1: R1.pin_1, ADC.pin8, R9.Pin_0
  N2: Nozzle_Heater.Pin_0, Q1.D
  12V: Nozzle_Heater.Pin_1, HeadBed_A.Pin_1, HeadBed_B.Pin_1, Pololu_A6.VOLTAGE_ST/_MT, Pololu_A7.VOLTAGE_ST/_MT, Pololu_A8.VOLTAGE_ST/_MT, Pololu_A9.VOLTAGE_ST/_MT
  N3: Q1.G, Raspberry_Pi_3_Model_b.GPIO21
  N4: Raspberry_Pi_3_Model_b.GPIO2, ADC.pin10, R4.Pin_1
  N5: Raspberry_Pi_3_Model_b.GPIO3, ADC.pin9, R3.Pin_1
  N6: Raspberry_Pi_3_Model_b.GPIO4, U4.DS
  N7: Raspberry_Pi_3_Model_b.GPIO17, U3.ST_CP, U4.ST_CP
  N8: Raspberry_Pi_3_Model_b.GPIO27, U3.SH_CP, U4.SH_CP
  N9: Raspberry_Pi_3_Model_b.GPIO22, U3.MR, U4.MR
  N10: Raspberry_Pi_3_Model_b.GPIO5, S2.O
  N11: Raspberry_Pi_3_Model_b.GPIO6, S3.O
  N12: Raspberry_Pi_3_Model_b.GPIO13, S4.O
  N13: Raspberry_Pi_3_Model_b.GPIO19, S6.O
  N14: Raspberry_Pi_3_Model_b.GPIO26, S5.O
  N15: Raspberry_Pi_3_Model_b.GPIO20, Q3.G, R6.Pin_1
  N16: Raspberry_Pi_3_Model_b.GPIO16, Q2.G, R5.Pin_1
  N17: Raspberry_Pi_3_Model_b.GPIO12, S1.O
  N18: ADC.pin6, R8.pin_1, R11.Pin_0
  N19: ADC.pin7, R7.pin_1, R10.Pin_0
  3.3V: ADC.pin14, ADC.pin16, R3.Pin_0, R4.Pin_0, R9.Pin_1, R10.Pin_1, R11.Pin_1, Pololu_A6.VOLTAGE_DD, Pololu_A7.VOLTAGE_DD, Pololu_A8.VOLTAGE_DD, Pololu_A9.VOLTAGE_DD, R12.Pin_0, R13.Pin_0, R14.Pin_0, R15.Pin_0, R16.Pin_0, R17.Pin_0, U3.VCC, U4.VCC
  N20: HeadBed_A.Pin_0, Q2.D
  N21: HeadBed_B.Pin_0, Q3.D
  AQ0: Pololu_A6.ENABLE, Pololu_A7.ENABLE, Pololu_A8.ENABLE, Pololu_A9.ENABLE
  AQ3: Pololu_A6.MS1, Pololu_A7.MS1, Pololu_A8.MS1, Pololu_A9.MS1
  AQ4: Pololu_A6.MS2, Pololu_A7.MS2, Pololu_A8.MS2, Pololu_A9.MS2
  AQ5: Pololu_A6.MS3, Pololu_A7.MS3, Pololu_A8.MS3, Pololu_A9.MS3
  AQ1: Pololu_A6.RESET, Pololu_A7.RESET, Pololu_A8.RESET, Pololu_A9.RESET
  AQ2: Pololu_A6.SLEEP, Pololu_A7.SLEEP, Pololu_A8.SLEEP, Pololu_A9.SLEEP
  AQ6: Pololu_A6.STEP
  AQ7: Pololu_A6.DIRECTION
  N22: Pololu_A6.OUT_2B, Y5.D
  N23: Pololu_A6.OUT_2A, Y5.B
  N24: Pololu_A6.OUT_1A, Y5.A
  N25: Pololu_A6.OUT_1B, Y5.C
  BQ0: Pololu_A7.STEP
  BQ1: Pololu_A7.DIRECTION
  N26: Pololu_A7.OUT_2B, Y6.D
  N27: Pololu_A7.OUT_2A, Y6.B
  N28: Pololu_A7.OUT_1A, Y6.A
  N29: Pololu_A7.OUT_1B, Y6.C
  BQ4: Pololu_A8.STEP
  BQ5: Pololu_A8.DIRECTION
  N30: Pololu_A8.OUT_2B, Y7.D
  N31: Pololu_A8.OUT_2A, Y7.B
  N32: Pololu_A8.OUT_1A, Y7.A
  N33: Pololu_A8.OUT_1B, Y7.C
  BQ2: Pololu_A9.STEP
  BQ3: Pololu_A9.DIRECTION
  N34: Pololu_A9.OUT_2B, Y8.D
  N35: Pololu_A9.OUT_2A, Y8.B
  N36: Pololu_A9.OUT_1A, Y8.A
  N37: Pololu_A9.OUT_1B, Y8.C
  N38: R12.Pin_1, S1.P
  N39: R13.Pin_1, S2.P
  N40: R14.Pin_1, S3.P
  N41: R15.Pin_1, S4.P
  N42: R16.Pin_1, S6.P
  N43: R17.Pin_1, S5.P
  drv reset: U3.Q1
  drv sleep: U3.Q2
  drv ms1: U3.Q3
  drv ms2: U3.Q4
  drv ms3: U3.Q5
  drv x step: U3.Q6
  drv x dir: U3.Q7
  N44: U3.DS, U4.Q7'
  drv enable: U3.Q0
  drv y dir: U4.Q1
  drv z step: U4.Q2
  drv z dir: U4.Q3
  drv e step: U4.Q4
  drv e dir: U4.Q5
  drv y step: U4.OE
